# Fritzing sketch pico_oled (saved by Fritzing 0.9.3b)
breadboards: 1

parts:
  OLED1 = OLED 128x64 I2C Monochrome Display GND-VDD
  Mod2 = Raspberry Pi Pico

nets:
  N1: OLED1.GND, Mod2.pin_3, Mod2.pin_8, Mod2.pin_13, Mod2.pin_18, Mod2.pin_23, Mod2.pin_28, Mod2.pin_33, Mod2.pin_38, Mod2.pin_42
  N2: OLED1.VDD, Mod2.pin_36
  N3: OLED1.SCK, Mod2.pin_10
  N4: OLED1.SDA, Mod2.pin_9

custom parts:
  OLED 128x64 I2C Monochrome Display GND-VDD: OLED 128x64 I2C Monochrome Display. Note: there are two variants of this part, this one is the GND VDD SCK SDA variant. The other is VDD GND SCK SDA. Make sure you select the part that matches your module as using the incorrect part will probably destroy your module! In addition the mounting holes are marked on silkscreen but not by default drilled. If you want drilled mounting holes, copy a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
  Raspberry Pi Pico: Raspberry Pi Pico. Based around the RP2040 microcontroller the Pico is a low cost microcontroller device bringing Raspberry Pi quality, cost, and easy of use to the microcontroller space. Jan 2021, Split part in to two versions: tht (this one) and SMD. This one will drill holes for a .1 in header in pcb to allow plugging in the module as well as providing pads to solder the module to the top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
